# Fritzing sketch Circuit (saved by Fritzing 0.9.6b)
circuit board: 8.46667cm x 5.64444cm
breadboards: 1

parts:
  R1 = Resistor [tolerance=±5% power=0.25 resistance=2.2k package=THT]
  S1 = Square Pushbutton
  Componente1 = Arduino Uno (Rev3) - ICSP
  J1 = Dagu DGServo 9g header (male) [package=THT]
  JP1 = Header 4 [package=screwterminal-3.5mm-4_lock]  # not connected
  JP2 = Header 4 [package=screwterminal-3.5mm-4_lock]
  JP3 = Header 3 [package=screwterminal-3.5mm-3_lock.007s]  # not connected

nets:
  GND: R1.Pin_0, Componente1.GND, J1.gnd
  N1: R1.Pin_1, S1.leg1, Componente1.D3_PWM
  N2: S1.leg0, Componente1.5V, JP2.4
  N3: Componente1.D5_PWM, J1.pulse
  VIN: Componente1.VIN, J1.Vcc
